// Logisim project ULA4_core.circ as structural Verilog
module main (
  input  [3:0] A,
  input  C,
  input  [3:0] B,
  input  V,
  input  [3:0] OP,
  input  Z,
  output [7:0] F
);
endmodule

module my_xor (
  input  A,
  input  B,
  output F
);

  wire and_1_out, and_2_out, not_1_out, not_2_out;

  not not_1 (not_1_out, A);
  not not_2 (not_2_out, B);
  and and_1 (and_1_out, A, not_2_out);
  and and_2 (and_2_out, not_1_out, B);
  or or_1 (F, and_1_out, and_2_out);
endmodule

module bin2gray4 (
  input  [3:0] A,
  output [3:0] F
);

  my_xor my_xor_1 (.A(A[1]), .B(A[0]), .F(F[0]));
  my_xor my_xor_2 (.A(A[2]), .B(A[1]), .F(F[1]));
  my_xor my_xor_3 (.A(A[3]), .B(A[2]), .F(F[2]));

  assign F[3] = A[3];
endmodule

module parity8_gen (
  input  [7:0] A,
  output P
);

  wire my_xor_1_f, my_xor_2_f, my_xor_3_f, my_xor_4_f, my_xor_5_f, my_xor_6_f;

  my_xor my_xor_1 (.A(A[0]), .B(A[1]), .F(my_xor_1_f));
  my_xor my_xor_2 (.A(my_xor_1_f), .B(A[2]), .F(my_xor_2_f));
  my_xor my_xor_3 (.A(my_xor_2_f), .B(A[3]), .F(my_xor_3_f));
  my_xor my_xor_4 (.A(my_xor_3_f), .B(A[4]), .F(my_xor_4_f));
  my_xor my_xor_5 (.A(my_xor_4_f), .B(A[5]), .F(my_xor_5_f));
  my_xor my_xor_6 (.A(my_xor_5_f), .B(A[6]), .F(my_xor_6_f));
  my_xor my_xor_7 (.A(my_xor_6_f), .B(A[7]), .F(P));
endmodule

module z_detect8_v1 (
  input  [7:0] A,
  output Z
);

  nor nor_1 (Z, A[0], A[1], A[2], A[3], A[4], A[5], A[6], A[7]);
endmodule
